# Fritzing sketch sylvia (saved by Fritzing 1.0.2b)
breadboards: 1

parts:
  A1 = Teensy 4.0
  R1 = Resistor [tolerance=±5% resistance=1M package="0603 [SMD]"]
  R2 = Resistor [tolerance=±5% resistance=1M package="0603 [SMD]"]
  U2 = AT42QT1012 [package=sot-23-6]
  U3 = AT42QT1012 [package=sot-23-6]  # not connected

nets:
  N1: A1.pin_1, A1.pin_32
  N2: A1.pin_4, R1.Pin_1, U2.TIME
  N3: A1.pin_5, R2.Pin_1
  N4: A1.pin_6, R1.Pin_0
  N5: A1.pin_8, R2.Pin_0

notes:
  these are capacitive touch sensors ->

custom parts:
  Teensy 4.0: The Teensy is a complete USB-based microcontoller development system, in a very small footprint, capable of implementing many types of projects. All programming is done via the USB port. No special programmer is needed, only a standard micro-USB cable and a PC or Macintosh with a USB port. (Oct 2023 added the VBUS pad at user request.)
